// Logisim project alu.circ as structural Verilog: 3 circuits, main circuit main
module ALU (
  input  [7:0] X,
  input  [7:0] Y,
  input  [2:0] OpCode,
  output OF,
  output [7:0] Output,
  output ZF,
  output SF,
  output CF,
  output EQ
);

  wire adder_1_cout, adder_2_cout, and_2_out, and_3_out, and_4_out, and_5_out, and_6_out, and_7_out,
       and_8_out, and_10_out, and_11_out, comparator_1_lt, not_2_out, not_3_out, not_4_out, of_1_s, of_2_s,
       or_2_out, or_3_out;
  wire [7:0] adder_1_out, adder_2_out, AND_out, bit_extender_1_out, not_1_out, OR_out, shifter_1_out,
       shifter_2_out, shifter_3_out;

  assign not_1_out = ~Y;  // NOT_Gate not_1, 8 bits wide
  assign OR_out = X | Y;  // OR_Gate OR, 8 bits wide
  assign AND_out = X & Y;  // AND_Gate AND, 8 bits wide
  Adder adder_1 (.a(X), .b(Y), .out(adder_1_out), .cin(1'b0), .cout(adder_1_cout));
  Adder adder_2 (.a(X), .b(not_1_out), .out(adder_2_out), .cin(1'b1), .cout(adder_2_cout));
  Comparator comparator_1 (.a(X), .b(Y), .lt(comparator_1_lt));  // open: gt, eq
  Shifter shifter_1 (.in(X), .\dist (Y[2:0]), .out(shifter_1_out));
  Shifter #(.shift("lr")) shifter_2 (.in(X), .\dist (Y[2:0]), .out(shifter_2_out));
  Shifter #(.shift("ar")) shifter_3 (.in(X), .\dist (Y[2:0]), .out(shifter_3_out));
  assign bit_extender_1_out = {{7{1'b0}}, comparator_1_lt};  // Bit_Extender bit_extender_1
  Comparator comparator_2 (.a(X), .b(Y), .eq(EQ));  // open: gt, lt
  Multiplexer #(.select(3), .width(8), .enable("false")) multiplexer_1 (
    .in0(OR_out), .in1(AND_out), .in2(adder_1_out), .in3(adder_2_out), .in4(shifter_1_out),
    .in5(shifter_2_out), .in6(shifter_3_out), .in7(bit_extender_1_out), .out(Output), .sel(OpCode));
  not not_2 (not_2_out, adder_2_cout);
  not not_3 (not_3_out, OpCode[2]);
  and and_2 (and_2_out, adder_1_cout, 1'b1);
  and and_3 (and_3_out, 1'b1, not_2_out);
  and and_4 (and_4_out, 1'b1, not_3_out);
  and and_5 (and_5_out, 1'b1, OpCode[1]);
  and and_6 (and_6_out, and_4_out, and_5_out);
  Comparator comparator_3 (.a(Output), .b({8{1'b0}}), .eq(ZF));  // open: gt, lt
  Comparator comparator_4 (.a(Output), .b({8{1'b0}}), .lt(SF));  // open: gt, eq
  OF of_1 (._1(X[7]), ._2(Y[7]), ._3(Output[7]), .S(of_1_s));
  OF of_2 (._1(Output[7]), ._2(Y[7]), ._3(X[7]), .S(of_2_s));
  not not_4 (not_4_out, OpCode[0]);
  and and_7 (and_7_out, not_4_out, and_2_out);
  and and_8 (and_8_out, OpCode[0], and_3_out);
  and and_9 (OF, and_6_out, or_3_out);
  and and_10 (and_10_out, OpCode[0], of_1_s);
  and and_11 (and_11_out, not_4_out, of_2_s);
  or or_2 (or_2_out, and_7_out, and_8_out);
  or or_3 (or_3_out, and_10_out, and_11_out);
  and and_12 (CF, and_6_out, or_2_out);
endmodule

module main (
  input  [2:0] op_code,
  input  [7:0] X,
  input  [7:0] Y,
  output [7:0] result,
  output SF,
  output ZF,
  output CF,
  output OF,
  output EQ
);

  ALU alu_1 (.X(X), .Y(Y), .OF(OF), .Output(result), .ZF(ZF), .SF(SF), .CF(CF), .EQ(EQ), .OpCode(op_code));

  // Notes on the sheet:
  //   CS 31 Lab 3, Part 2$$Please do NOT put$your names here.
endmodule

module OF (
  input  _1,
  input  _2,
  input  _3,
  output S
);

  wire not_1_out, xor_1_out, xor_2_out;

  xor xor_1 (xor_1_out, _2, _3);
  xor xor_2 (xor_2_out, _1, _2);
  not not_1 (not_1_out, xor_1_out);
  and and_1 (S, xor_2_out, not_1_out);
endmodule
