// Logisim project part1.circ as structural Verilog: 5 circuits, main circuit main
module main (
  input  [3:0] X,
  input  [1:0] Y,
  input  CarryIn,
  output [3:0] Sum,
  output CarryOut
);

  wire [3:0] signext2to4_1_out_2;

  signext2to4 signext2to4_1 (.Input(Y), .out_2(signext2to4_1_out_2));
  fulladder4 fulladder4_1 (.X(X), .Y(signext2to4_1_out_2), .CarryIn(CarryIn), .Sum(Sum), .CarryOut(CarryOut));

  // Notes on the sheet:
  //   CS31 Lab 3, Part 1$$Please do NOT put$your names here.
endmodule

module signext2to4 (
  input  [1:0] Input,
  output [3:0] out_2
);


  assign out_2 = {{3{Input[1]}}, Input[0]};
endmodule

module fulladder (
  input  X,
  input  Y,
  input  CarryIn,
  output Sum,
  output CarryOut
);

  wire and_1_out, and_2_out, xor_1_out_3;

  XOR xor_1 (.in_1(X), .in_2(Y), .out_3(xor_1_out_3));
  and and_1 (and_1_out, X, Y);
  XOR xor_2 (.in_1(xor_1_out_3), .in_2(CarryIn), .out_3(Sum));
  and and_2 (and_2_out, xor_1_out_3, CarryIn);
  or or_1 (CarryOut, and_2_out, and_1_out);
endmodule

module XOR (
  input  in_1,
  input  in_2,
  output out_3
);

  wire and_1_out, and_2_out, not_1_out, not_2_out;

  not not_1 (not_1_out, in_1);
  and and_1 (and_1_out, not_1_out, in_2);
  and and_2 (and_2_out, in_1, not_2_out);
  not not_2 (not_2_out, in_2);
  or or_1 (out_3, and_1_out, and_2_out);
endmodule

module fulladder4 (
  input  [3:0] X,
  input  [3:0] Y,
  input  CarryIn,
  output [3:0] Sum,
  output CarryOut
);

  wire fulladder_1_carryout, fulladder_2_carryout, fulladder_3_carryout;

  fulladder fulladder_1 (.X(X[0]), .Y(Y[0]), .CarryIn(CarryIn), .Sum(Sum[0]), .CarryOut(fulladder_1_carryout));
  fulladder fulladder_2 (
    .X(X[1]), .Y(Y[1]), .CarryIn(fulladder_1_carryout), .Sum(Sum[1]), .CarryOut(fulladder_2_carryout));
  fulladder fulladder_3 (
    .X(X[2]), .Y(Y[2]), .CarryIn(fulladder_2_carryout), .Sum(Sum[2]), .CarryOut(fulladder_3_carryout));
  fulladder fulladder_4 (.X(X[3]), .Y(Y[3]), .CarryIn(fulladder_3_carryout), .Sum(Sum[3]), .CarryOut(CarryOut));
endmodule
